# Fritzing sketch Web-bed (saved by Fritzing 0.9.0b)
breadboards: 1

parts:
  Q1 = Basic FET N-Channel [package="TO220 [THT]"]
  Q2 = Basic FET N-Channel [package="TO220 [THT]"]
  Q3 = Basic FET N-Channel [package="TO220 [THT]"]
  JP1 = Header 4 [package=jst-4-pth]
  IR1 = TSOP312.., 314.. [package=THT]

nets:
  N1: Q1.drain, JP1.2
  GND: Q1.source, Q2.source, Q3.source, IR1.GND
  N2: Q2.drain, JP1.3
  N3: Q3.drain, JP1.4
  12V: JP1.1
  3.3V: IR1.Vs
